# Fritzing sketch pitch_connections (saved by Fritzing 0.9.3b)

parts:
  Part1 = Arduino Uno (Rev3) - ICSP
  Part2 = Tri-Axis Gyro Breakout - L3G4200D
  Grove1 = Grove OLED 128x96
  SM3 = 28BYJ-48 Stepper Motor [part_number=28BYJ-48]  # not connected
  Driver3 = 28BYJ-48 Driver Module [part_number=ULN2003 package=THT]

nets:
  N1: Part1.A4/SDA, Part2.SDA, Grove1.SDA
  N2: Part1.A5/SCL, Part2.SCL, Grove1.SCL
  N3: Part1.D8, Driver3.IN1
  N4: Part1.D9_PWM, Driver3.IN2
  N5: Part1.D10_PWM/SS, Driver3.IN3
  N6: Part1.D11_PWM/MOSI, Driver3.IN4
  GND: Part1.GND, Part2.GND
  VCC: Part2.VCC, Grove1.VCC

notes:
  Pitch Mechanism Connections

custom parts:
  28BYJ-48 Stepper Motor: Unipolar Stepper Motor 28BYJ-48 Top coil - pink & orange Bottom coil - blue & yellow Common rail - red Connector pins: blue - pink - yellow - orange - red
  28BYJ-48 Driver Module: Generic male header
