# Fritzing sketch yaw_connections (saved by Fritzing 0.9.3b)

parts:
  Part1 = Arduino Uno (Rev3) - ICSP
  Driver3 = 28BYJ-48 Driver Module [part_number=ULN2003 package=THT]
  SM3 = 28BYJ-48 Stepper Motor [part_number=28BYJ-48]

nets:
  N1: Part1.D8, Driver3.IN1
  N2: Part1.D9_PWM, Driver3.IN2
  N3: Part1.D10_PWM/SS, Driver3.IN3
  N4: Part1.D11_PWM/MOSI, Driver3.IN4
  GND: Part1.GND, Driver3.GND
  N5: Part1.5V, Driver3.Vmotor
  N6: Driver3.blue-pin, SM3.blue-pin
  N7: Driver3.pink-pin, SM3.pink-pin
  N8: Driver3.yellow-pin, SM3.yellow-pin
  N9: Driver3.orange-pin, SM3.orange-pin
  N10: Driver3.red-pin, SM3.red-pin

notes:
  Yaw Mechanism connections

custom parts:
  28BYJ-48 Driver Module: Generic male header
  28BYJ-48 Stepper Motor: Unipolar Stepper Motor 28BYJ-48 Top coil - pink & orange Bottom coil - blue & yellow Common rail - red Connector pins: blue - pink - yellow - orange - red
